# Fritzing sketch schema (saved by Fritzing 0.9.3b)
breadboards: 1

parts:
  R1 = Photocell (LDR) [package=THT]
  R2 = Photocell (LDR) [package=THT]
  R3 = Resistor [tolerance=±5% resistance=10k package="0603 [SMD]"]
  R4 = Resistor [tolerance=±5% resistance=10k package="0603 [SMD]"]
  U1 = ESP32-38PinWide [part_number=ESP32-38PinWide]
  J1 = Basic Servo

nets:
  N1: R1.pin_0, R3.Pin_1, U1.GPIO34
  GND: R1.pin_1, R2.pin_1, U1.GND, J1.gnd
  N2: R2.pin_0, R4.Pin_1, U1.GPIO35
  N3: R3.Pin_0, R4.Pin_0, U1.3.3, J1.vcc

custom parts:
  ESP32-38PinWide: Generic 38-Pin ESP32 with wide format (only access to one side of pins on a breadboard) based on Stephen Lilley's HiLetgo ESP-WROOM-32 ESP32 ESP-32S Development Board.
